# Fritzing sketch main-module-Arduino-Mega (saved by Fritzing 0.9.3b)
circuit board: 8.46667cm x 5.64444cm
breadboards: 1

parts:
  Part1 = Arduino Mega 2560 (Rev3)
  HC-1 = HC-12 Module
  OLED_I2C1 = OLED 128x64 I2C Monochrome Display
  M1 = fc-51 [package=THT]
  Antenna1 = HC-12 Antenna

nets:
  N1: Part1.D21/SCL, OLED_I2C1.SCK
  N2: Part1.D20/SDA, OLED_I2C1.SDA
  5V: Part1.5V, HC-1.VCC, OLED_I2C1.VDD, M1.pin3
  GND: Part1.GND, HC-1.GND, OLED_I2C1.GND, M1.pin2
  N3: Part1.D2_PWM, M1.pin1
  N4: Part1.D46, HC-1.RXD
  N5: Part1.D48, HC-1.TXD
  N6: HC-1.ANT, Antenna1.ANT

custom parts:
  HC-12 Module: HC-12 433Mhz Module
  HC-12 Antenna: Antenna for HC-12 433Mhz Module
